# Fritzing sketch VisualEar (saved by Fritzing 0.8.7b)
breadboards: 1

parts:
  LPD8806_RGB_LED_Strip1 = LPD8806 RGB LED Strip
  Part1 = Adafruit I2S Mic - SPH0645 [part_number="Adafruit #3421"]
  U1 = ESP32-38PinWide [part_number=ESP32-38PinWide]
  JACK1 = 2.1mm DC Barrel Jack

nets:
  GND: LPD8806_RGB_LED_Strip1.GND, Part1.GND, U1.GND, JACK1.switch
  N1: LPD8806_RGB_LED_Strip1.DI, U1.GPIO12
  N2: LPD8806_RGB_LED_Strip1.CI, U1.GPIO14
  N3: Part1.VDD, U1.3.3
  N4: Part1.BCLK, U1.GPIO26
  N5: Part1.DATA, U1.GPIO25
  N6: Part1.WS, U1.GPIO33
  N7: U1.VIN, JACK1.center

notes:
  Visual Ear,
  by Phil Malone 2020

custom parts:
  LPD8806 RGB LED Strip: Digitally addressable RGB LED strip
  Adafruit I2S Mic - SPH0645: For many microcontrollers, adding audio input is easy with one of our analog microphone breakouts. But as you get to bigger and better microcontrollers and microcomputers, you'll find that you don't always have an analog input, or maybe you want to avoid the noise that can seep in with an analog mic system. Once you get past 8-bit micros, you will often find an I2S peripheral, that can take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
  ESP32-38PinWide: Generic 38-Pin ESP32 with wide format (only access to one side of pins on a breadboard) based on Stephen Lilley's HiLetgo ESP-WROOM-32 ESP32 ESP-32S Development Board.
  2.1mm DC Barrel Jack: 2.1mm DC Barrel Jack with Thru-Hole Connectors (breadboardable)
